# Fritzing sketch Connections (saved by Fritzing 0.9.3b)

parts:
  S1 = Pushbutton [package="[SMD]"]
  Raspberry_Pi_1 = Raspberry Pi 3 [part_number=RPI-3-V1.2]
  M1 = DC Motor
  J1 = Power Jack [package=power_jack_slot]
  KY-1 = Keyes Relay [package=THT]

nets:
  GND: S1.Pin_1, Raspberry_Pi_1.GND, J1.GND, KY-1.ground, KY-1.C
  N1: S1.Pin_3, S1.Pin_4, Raspberry_Pi_1.GIPO20
  N2: Raspberry_Pi_1.3v3, KY-1.power
  N3: Raspberry_Pi_1.GIPO4, KY-1.signal
  N4: M1.pin_1, KY-1.NO
  N5: M1.pin_2, J1.GNDBREAK

notes:
  Camera

custom parts:
  Keyes Relay: The Keyes 5V relay module is suitable for SCM development, home appliance control. It uses a 5V~12V TIL control signal which can control DC / AC signal.
